# Fritzing sketch badge (saved by Fritzing 0.9.3b)
breadboards: 1

parts:
  Part1 = Adafruit Feather M0 Adalogger [part_number="Adafruit #2796"]
  WaveShare_1_3inch_OLED_128x1 = WaveShare 1.3inch OLED 128x64
  NEXT = Pushbutton [package="[SMD]"]

nets:
  GND: Part1.GND, WaveShare_1_3inch_OLED_128x1.GND, NEXT.Pin_3, NEXT.Pin_4
  N1: Part1.MOSI, WaveShare_1_3inch_OLED_128x1.DIN
  N2: Part1.SCK, WaveShare_1_3inch_OLED_128x1.CLK
  N3: Part1.A5, WaveShare_1_3inch_OLED_128x1.CS
  N4: Part1.A4, WaveShare_1_3inch_OLED_128x1.D/C
  N5: Part1.A3, WaveShare_1_3inch_OLED_128x1.RES
  N6: Part1.A2, WaveShare_1_3inch_OLED_128x1.BUSY
  N7: Part1.A1, NEXT.Pin_1, NEXT.Pin_2
  +3V3: Part1.+3V3, WaveShare_1_3inch_OLED_128x1.VCC

custom parts:
  Adafruit Feather M0 Adalogger: This is the Adafruit Feather M0 Adalogger - our take on an 'all-in-one' Cortex M0 datalogger (or data-reader) with built in USB and battery charging. Its an Adafruit Feather M0 with a microSD holder ready to rock! We have other boards in the Feather family, check'em out here At the Feather M0's heart is an ATSAMD21G18 ARM Cortex M0 processor, clocked at 48 MHz and at 3.3V logic, the same one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
  WaveShare 1.3inch OLED 128x64: OLED Original design by Simulz (http://tsblog.simulz.kr) Corrected PCB layout by Andreas Horneffer
